# Fritzing sketch 線路圖 (saved by Fritzing 1.0.2b)
breadboards: 1

parts:
  KY-1 = Keyes Relay [package=THT]
  Mod1 = Raspberry Pi 4B
  DHT11_1 = DHT11 module

nets:
  N1: KY-1.signal, Mod1.GPIO18
  5V: KY-1.power, Mod1.5V, DHT11_1.VCC
  GND: KY-1.ground, Mod1.GND, DHT11_1.GND
  N2: Mod1.GPIO27, DHT11_1.DATA

custom parts:
  Keyes Relay: The Keyes 5V relay module is suitable for SCM development, home appliance control. It uses a 5V~12V TIL control signal which can control DC / AC signal.
  DHT11 module: DHT11 black pcb module
